// Logisim project processador_Bruno.circ as structural Verilog: 3 circuits, main circuit main
module main (
  input  in_1,
  input  in_2,
  input  in_3,
  output out_4,
  output out_5
);

  ADD_1 add_1_1 (.a(in_2), .b(in_1), .vem_1(in_3), .s(out_5), .vai_1(out_4));
endmodule

module ADD_1 (
  input  a,
  input  b,
  input  vem_1,
  output s,
  output vai_1
);

  wire and_1_out, and_2_out, or_1_out, xor_1_out;

  xor xor_1 (xor_1_out, a, b);
  or or_1 (or_1_out, b, vem_1);
  and and_1 (and_1_out, b, vem_1);
  xor xor_2 (s, xor_1_out, vem_1);
  and and_2 (and_2_out, or_1_out, a);
  or or_2 (vai_1, and_2_out, and_1_out);
endmodule

module ADD_4 (
  input  [3:0] B,
  input  [3:0] A,
  input  Vem_1,
  output Vai_1,
  output [3:0] S
);

  wire add_1_2_vai_1, add_1_3_vai_1, add_1_4_vai_1;

  ADD_1 add_1_1 (.a(B[3]), .b(A[3]), .vem_1(add_1_2_vai_1), .s(S[3]), .vai_1(Vai_1));
  ADD_1 add_1_2 (.a(B[2]), .b(A[2]), .vem_1(add_1_3_vai_1), .s(S[2]), .vai_1(add_1_2_vai_1));
  ADD_1 add_1_3 (.a(B[1]), .b(A[1]), .vem_1(add_1_4_vai_1), .s(S[1]), .vai_1(add_1_3_vai_1));
  ADD_1 add_1_4 (.a(B[0]), .b(A[0]), .vem_1(Vem_1), .s(S[0]), .vai_1(add_1_4_vai_1));
endmodule
